// Logisim project RegisterFiles.circ as structural Verilog: 3 circuits, main circuit main
module main (
  input  mem_write_en,
  input  reg_write_en,
  input  [1:0] access_size,
  input  [31:0] rd_data_in,
  input  [4:0] rd_addr,
  input  [31:0] addr,
  input  [4:0] rs1_addr,
  input  [4:0] rs2_addr,
  input  [31:0] write_data,
  output [31:0] rs1_data,
  output [31:0] read_data,
  output [31:0] rs2_data
);

  wire clk;

  Register_File register_file_1 (
    .reg_write_en(reg_write_en), .clk(clk), .rd_data_in(rd_data_in), .rd_addr(rd_addr), .rs1_addr(rs1_addr),
    .rs2_addr(rs2_addr), .rs1_data(rs1_data), .rs2_data(rs2_data));
  Clock u_clk (.out(clk));
  Data_memory data_memory_1 (
    .mem_write_en(mem_write_en), .access_size(access_size), .clk(clk), .addr(addr), .write_data(write_data),
    .read_data(read_data));

  // Notes on the sheet:
  //   LAB 03
  //   Name: Sadiksha Lamsal
  //   Date: 4/28/2026
endmodule

module Data_memory (
  input  mem_write_en,
  input  [1:0] access_size,
  input  clk,
  input  [31:0] addr,
  input  [31:0] write_data,
  output [31:0] read_data
);

  wire and_1_out, and_2_out, comparator_1_eq, comparator_2_eq, decoder_1_out0, decoder_1_out1,
       decoder_1_out2, decoder_1_out3, not_1_out, or_1_out, or_2_out, or_3_out, or_4_out, W0, W1, W2, W3;
  wire [7:0] D0, D1, D2, D3, multiplexer_2_out;
  wire [15:0] multiplexer_1_out;
  wire [31:0] bit_extender_2_out, halfword;

  RAM #(.addrWidth(24), .databus("bibus")) ram_1 (
    .addr(addr[25:2]), .we(W0), .oe(1'b1), .clk(clk), .din(write_data[7:0]), .dout(D0));
  Multiplexer #(.width(16), .enable("false")) multiplexer_1 (
    .in0({D1, D0}), .in1({D3, D2}), .out(multiplexer_1_out), .sel(addr[1]));
  assign halfword = {{16{multiplexer_1_out[15]}}, multiplexer_1_out};  // Bit_Extender bit_extender_1
  // Probe on D0
  RAM #(.addrWidth(24), .databus("bibus")) ram_2 (
    .addr(addr[25:2]), .we(W1), .oe(1'b1), .clk(clk), .din(write_data[15:8]), .dout(D1));
  Comparator #(.width(2)) comparator_1 (.a(access_size), .b(2'b01), .eq(comparator_1_eq));  // open: gt, lt
  Decoder #(.select(2)) decoder_1 (
    .out0(decoder_1_out0), .out1(decoder_1_out1), .out2(decoder_1_out2), .out3(decoder_1_out3),
    .sel(addr[1:0]));  // open: en
  // Probe on D1
  not not_1 (not_1_out, addr[1]);
  Comparator #(.width(2)) comparator_2 (.a(access_size), .b(2'b10), .eq(comparator_2_eq));  // open: gt, lt
  and and_1 (and_1_out, comparator_1_eq, not_1_out);
  and and_2 (and_2_out, comparator_1_eq, addr[1]);
  RAM #(.addrWidth(24), .databus("bibus")) ram_3 (
    .addr(addr[25:2]), .we(W2), .oe(1'b1), .clk(clk), .din(write_data[23:16]), .dout(D2));
  or or_1 (or_1_out, decoder_1_out0, and_1_out, comparator_2_eq);
  or or_2 (or_2_out, decoder_1_out1, and_1_out, comparator_2_eq);
  or or_3 (or_3_out, decoder_1_out2, and_2_out, comparator_2_eq);
  or or_4 (or_4_out, decoder_1_out3, and_2_out, comparator_2_eq);
  and and_3 (W0, or_1_out, mem_write_en);
  and and_4 (W1, or_2_out, mem_write_en);
  and and_5 (W2, or_3_out, mem_write_en);
  and and_6 (W3, or_4_out, mem_write_en);
  Multiplexer #(.select(2), .width(8), .enable("false")) multiplexer_2 (
    .in0(D0), .in1(D1), .in2(D2), .in3(D3), .out(multiplexer_2_out), .sel(addr[1:0]));
  // Probe on D2
  RAM #(.addrWidth(24), .databus("bibus")) ram_4 (
    .addr(addr[25:2]), .we(W3), .oe(1'b1), .clk(clk), .din(write_data[31:24]), .dout(D3));
  assign bit_extender_2_out = {{24{multiplexer_2_out[7]}}, multiplexer_2_out};  // Bit_Extender bit_extender_2
  Multiplexer #(.select(2), .width(32), .enable("false")) multiplexer_3 (
    .in0(bit_extender_2_out), .in1(halfword), .in2({D3, D2, D1, D0}), .out(read_data), .sel(access_size));  // open: in3
  // Probe on D3

  // Other names for the same wires on the sheet: addr01[1:0] = addr[1:0]; raw_word[31:0] = {D3, D2, D1, D0};
  //   WD0[7:0] = write_data[7:0]; WD1[7:0] = write_data[15:8]; WD2[7:0] = write_data[23:16];
  //   WD3[7:0] = write_data[31:24]

  // Notes on the sheet:
  //   DATA MEMORY
endmodule

module Register_File (
  input  reg_write_en,
  input  clk,
  input  [31:0] rd_data_in,
  input  [4:0] rd_addr,
  input  [4:0] rs1_addr,
  input  [4:0] rs2_addr,
  output [31:0] rs1_data,
  output [31:0] rs2_data
);

  wire and_1_out, and_2_out, and_3_out, and_4_out, and_5_out, and_6_out, and_7_out, and_8_out, and_9_out,
       and_10_out, and_11_out, and_12_out, and_13_out, and_14_out, and_15_out, and_16_out, and_17_out,
       and_18_out, and_19_out, and_20_out, and_21_out, and_22_out, and_23_out, and_24_out, and_25_out,
       and_26_out, and_27_out, and_28_out, and_29_out, and_30_out, and_31_out, s1, s2, s3, s4, s5, s6, s7,
       s8, s9, s10, s11, s12, s13, s14, s15, s16, s17, s18, s19, s20, s21, s22, s23, s24, s25, s26, s27, s28,
       s29, s30, s31;
  wire [31:0] r1, r2, r3, r4, r5, r6, r7, r8, r9, r10, r11, r12, r13, r14, r15, r16, r17, r18, r19, r20, r21,
       r22, r23, r24, r25, r26, r27, r28, r29, r30, r31;

  Decoder #(.select(5)) decoder_1 (
    .out1(s1), .out2(s2), .out3(s3), .out4(s4), .out5(s5), .out6(s6), .out7(s7), .out8(s8), .out9(s9),
    .out10(s10), .out11(s11), .out12(s12), .out13(s13), .out14(s14), .out15(s15), .out16(s16), .out17(s17),
    .out18(s18), .out19(s19), .out20(s20), .out21(s21), .out22(s22), .out23(s23), .out24(s24), .out25(s25),
    .out26(s26), .out27(s27), .out28(s28), .out29(s29), .out30(s30), .out31(s31), .sel(rd_addr));  // open: out0, en
  and and_1 (and_1_out, reg_write_en, s1);
  and and_2 (and_2_out, reg_write_en, s2);
  and and_3 (and_3_out, reg_write_en, s3);
  and and_4 (and_4_out, reg_write_en, s4);
  and and_5 (and_5_out, reg_write_en, s5);
  and and_6 (and_6_out, reg_write_en, s6);
  and and_7 (and_7_out, reg_write_en, s7);
  Register #(.width(32)) x1 (.D(rd_data_in), .en(and_1_out), .clk(clk), .Q(r1));  // open: clr
  Register #(.width(32)) x2 (.D(rd_data_in), .en(and_2_out), .clk(clk), .Q(r2));  // open: clr
  Register #(.width(32)) x3 (.D(rd_data_in), .en(and_3_out), .clk(clk), .Q(r3));  // open: clr
  Register #(.width(32)) x4 (.D(rd_data_in), .en(and_4_out), .clk(clk), .Q(r4));  // open: clr
  Register #(.width(32)) x5 (.D(rd_data_in), .en(and_5_out), .clk(clk), .Q(r5));  // open: clr
  Register #(.width(32)) x6 (.D(rd_data_in), .en(and_6_out), .clk(clk), .Q(r6));  // open: clr
  Register #(.width(32)) x7 (.D(rd_data_in), .en(and_7_out), .clk(clk), .Q(r7));  // open: clr
  Multiplexer #(.select(5), .width(32), .enable("false")) multiplexer_1 (
    .in0({32{1'b0}}), .in1(r1), .in2(r2), .in3(r3), .in4(r4), .in5(r5), .in6(r6), .in7(r7), .in8(r8),
    .in9(r9), .in10(r10), .in11(r11), .in12(r12), .in13(r13), .in14(r14), .in15(r15), .in16(r16), .in17(r17),
    .in18(r18), .in19(r19), .in20(r20), .in21(r21), .in22(r22), .in23(r23), .in24(r24), .in25(r25),
    .in26(r26), .in27(r27), .in28(r28), .in29(r29), .in30(r30), .in31(r31), .out(rs1_data), .sel(rs1_addr));
  Register #(.width(32)) x8 (.D(rd_data_in), .en(and_8_out), .clk(clk), .Q(r8));  // open: clr
  and and_8 (and_8_out, reg_write_en, s8);
  Register #(.width(32)) x9 (.D(rd_data_in), .en(and_9_out), .clk(clk), .Q(r9));  // open: clr
  and and_9 (and_9_out, reg_write_en, s9);
  and and_10 (and_10_out, reg_write_en, s10);
  Register #(.width(32)) x11 (.D(rd_data_in), .en(and_11_out), .clk(clk), .Q(r11));  // open: clr
  and and_11 (and_11_out, reg_write_en, s11);
  Register #(.width(32)) x12 (.D(rd_data_in), .en(and_12_out), .clk(clk), .Q(r12));  // open: clr
  and and_12 (and_12_out, reg_write_en, s12);
  and and_13 (and_13_out, reg_write_en, s13);
  Register #(.width(32)) x14 (.D(rd_data_in), .en(and_14_out), .clk(clk), .Q(r14));  // open: clr
  and and_14 (and_14_out, reg_write_en, s14);
  and and_15 (and_15_out, reg_write_en, s15);
  Register #(.width(32)) x10 (.D(rd_data_in), .en(and_10_out), .clk(clk), .Q(r10));  // open: clr
  Register #(.width(32)) x13 (.D(rd_data_in), .en(and_13_out), .clk(clk), .Q(r13));  // open: clr
  Register #(.width(32)) x15 (.D(rd_data_in), .en(and_15_out), .clk(clk), .Q(r15));  // open: clr
  Multiplexer #(.select(5), .width(32), .enable("false")) multiplexer_2 (
    .in0({32{1'b0}}), .in1(r1), .in2(r2), .in3(r3), .in4(r4), .in5(r5), .in6(r6), .in7(r7), .in8(r8),
    .in9(r9), .in10(r10), .in11(r11), .in12(r12), .in13(r13), .in14(r14), .in15(r15), .in16(r16), .in17(r17),
    .in18(r18), .in19(r19), .in20(r20), .in21(r21), .in22(r22), .in23(r23), .in24(r24), .in25(r25),
    .in26(r26), .in27(r27), .in28(r28), .in29(r29), .in30(r30), .in31(r31), .out(rs2_data), .sel(rs2_addr));
  and and_16 (and_16_out, reg_write_en, s16);
  and and_17 (and_17_out, reg_write_en, s17);
  and and_18 (and_18_out, reg_write_en, s19);
  and and_19 (and_19_out, reg_write_en, s22);
  Register #(.width(32)) x16 (.D(rd_data_in), .en(and_16_out), .clk(clk), .Q(r16));  // open: clr
  Register #(.width(32)) x17 (.D(rd_data_in), .en(and_17_out), .clk(clk), .Q(r17));  // open: clr
  Register #(.width(32)) x18 (.D(rd_data_in), .en(and_20_out), .clk(clk), .Q(r18));  // open: clr
  and and_20 (and_20_out, reg_write_en, s18);
  Register #(.width(32)) x19 (.D(rd_data_in), .en(and_18_out), .clk(clk), .Q(r19));  // open: clr
  Register #(.width(32)) x20 (.D(rd_data_in), .en(and_21_out), .clk(clk), .Q(r20));  // open: clr
  and and_21 (and_21_out, reg_write_en, s20);
  Register #(.width(32)) x21 (.D(rd_data_in), .en(and_22_out), .clk(clk), .Q(r21));  // open: clr
  and and_22 (and_22_out, reg_write_en, s21);
  Register #(.width(32)) x22 (.D(rd_data_in), .en(and_19_out), .clk(clk), .Q(r22));  // open: clr
  Register #(.width(32)) x23 (.D(rd_data_in), .en(and_23_out), .clk(clk), .Q(r23));  // open: clr
  and and_23 (and_23_out, reg_write_en, s23);
  Register #(.width(32)) x24 (.D(rd_data_in), .en(and_24_out), .clk(clk), .Q(r24));  // open: clr
  and and_24 (and_24_out, reg_write_en, s24);
  Register #(.width(32)) x25 (.D(rd_data_in), .en(and_25_out), .clk(clk), .Q(r25));  // open: clr
  and and_25 (and_25_out, reg_write_en, s25);
  Register #(.width(32)) x26 (.D(rd_data_in), .en(and_26_out), .clk(clk), .Q(r26));  // open: clr
  and and_26 (and_26_out, reg_write_en, s26);
  Register #(.width(32)) x27 (.D(rd_data_in), .en(and_27_out), .clk(clk), .Q(r27));  // open: clr
  and and_27 (and_27_out, reg_write_en, s27);
  Register #(.width(32)) x28 (.D(rd_data_in), .en(and_28_out), .clk(clk), .Q(r28));  // open: clr
  and and_28 (and_28_out, reg_write_en, s28);
  Register #(.width(32)) x29 (.D(rd_data_in), .en(and_29_out), .clk(clk), .Q(r29));  // open: clr
  and and_29 (and_29_out, reg_write_en, s29);
  Register #(.width(32)) x30 (.D(rd_data_in), .en(and_30_out), .clk(clk), .Q(r30));  // open: clr
  and and_30 (and_30_out, reg_write_en, s30);
  Register #(.width(32)) x31 (.D(rd_data_in), .en(and_31_out), .clk(clk), .Q(r31));  // open: clr
  and and_31 (and_31_out, reg_write_en, s31);

  // Notes on the sheet:
  //   REGISTER FILE
endmodule
