// Logisim project ALU.circ as structural Verilog: 8 circuits, main circuit ALU_Test
module ALU_Test (
  output [31:0] result,
  output zero,
  output overflow,
  output carry_out
);

  wire clk;
  wire [3:0] Control_Register_q, Control_ROM_data, Count_q;
  wire [31:0] Register_A_q, Register_B_q, ROM_A_data, ROM_B_data;

  Clock sysclk ();  // open: out
  Counter #(.width(4), .max('hf)) Count (.clk(clk), .Q(Count_q));  // open: clr, load, up, count, D, carry
  Clock u_clk (.out(clk));
  ROM #(.addrWidth(4), .dataWidth(4)) Control_ROM (.addr(Count_q), .data(Control_ROM_data));
  Register #(.width(4)) Control_Register (
    .D(Control_ROM_data), .en(1'b1), .clk(clk), .Q(Control_Register_q));  // open: clr
  ROM #(.addrWidth(4), .dataWidth(32)) ROM_A (.addr(Count_q), .data(ROM_A_data));
  // Probe on Control_Register_q[2]
  // Probe on Register_A_q
  // Probe on Control_Register_q[1:0]
  Register #(.width(32)) Register_A (.D(ROM_A_data), .en(1'b1), .clk(clk), .Q(Register_A_q));  // open: clr
  // Probe on Register_B_q
  ROM #(.addrWidth(4), .dataWidth(32)) ROM_B (.addr(Count_q), .data(ROM_B_data));
  ALU_assembled alu_assembled_1 (
    .A(Register_A_q), .B(Register_B_q), .ShiftOp(Control_Register_q[3:2]),
    .isUnsigned(Control_Register_q[2]), .Add_SUB(Control_Register_q[2]), .LogicalOp(Control_Register_q[3:2]),
    .ALU_Selection(Control_Register_q[1:0]), .result(result), .Zero(zero), .overflow(overflow),
    .carry_out(carry_out));
  Register #(.width(32)) Register_B (.D(ROM_B_data), .en(1'b1), .clk(clk), .Q(Register_B_q));  // open: clr

  // Notes on the sheet:
  //   LAB 02: ALU
  //   Name: Sadiksha Lamsal
  //   Date: 4/19//2026
  //   TEST BENCH
  //   contents of Control_ROM (hex, n*v repeats v):
  //   0 4 8 c 1 2 2 6 3 7 b f
  //   contents of ROM_A (hex, n*v repeats v):
  //   4*aaaaaaa5 2 7fffffff 5 80000000 f0f0f0f0 f0f0f0f0 0 aaaaaaaa
  //   contents of ROM_B (hex, n*v repeats v):
  //   4*4 5 1 3 80000000 f0f0f0f f0f0f0f 0 55555555
endmodule

module final_ALU (
  input  [31:0] A,
  input  [31:0] B,
  input  [1:0] ShiftOp,
  input  UnsignedComparator,
  input  Add_Sub,
  input  [1:0] LogicalOp,
  input  [1:0] ALU_Selection,
  output [31:0] Result,
  output out_9,
  output overflow,
  output carry_out
);

  ALU_assembled alu_assembled_1 (
    .A(A), .B(B), .ShiftOp(ShiftOp), .isUnsigned(UnsignedComparator), .Add_SUB(Add_Sub),
    .LogicalOp(LogicalOp), .ALU_Selection(ALU_Selection), .result(Result), .Zero(out_9), .overflow(overflow),
    .carry_out(carry_out));

  // Notes on the sheet:
  //   ALU CIRCUIT
endmodule

module ALU_assembled (
  input  [31:0] A,
  input  [31:0] B,
  input  [1:0] ShiftOp,
  input  isUnsigned,
  input  Add_SUB,
  input  [1:0] LogicalOp,
  input  [1:0] ALU_Selection,
  output [31:0] result,
  output Zero,
  output overflow,
  output carry_out
);

  wire Comparator, not_1_out, or_1_out, or_2_out;
  wire [31:0] compare_1_out_5, logical_1_result, ripplecarryadder_1_final_output, shifts_1_out_4;

  or or_1 (or_1_out, Comparator, Add_SUB);
  and and_1 (Comparator, ALU_Selection[0], not_1_out);
  not not_1 (not_1_out, ALU_Selection[1]);
  Shifts shifts_1 (.Z(A), .ShiftAmount(B[4:0]), .ShiftOp(ShiftOp), .out_4(shifts_1_out_4));
  RippleCarryAdder ripplecarryadder_1 (
    .B(B), .ADD_SUB(or_1_out), .A(A), .final_output(ripplecarryadder_1_final_output), .Overflow(overflow),
    .Carry_out(carry_out));
  Logical logical_1 (.B(B), .A(A), .Operation(LogicalOp), .result(logical_1_result));
  Compare compare_1 (
    .Sign(ripplecarryadder_1_final_output[31]), .overflow(overflow), .carry_out(carry_out),
    .isUnsigned(isUnsigned), .out_5(compare_1_out_5));
  Multiplexer #(.select(2), .width(32), .enable("false")) multiplexer_1 (
    .in0(shifts_1_out_4), .in1(compare_1_out_5), .in2(ripplecarryadder_1_final_output),
    .in3(logical_1_result), .out(result), .sel(ALU_Selection));
  or or_2 (or_2_out, result[31], result[30], result[29], result[28], result[27], result[26], result[25], result[24], result[23], result[22], result[21], result[20], result[19], result[18], result[17], result[16], result[15], result[14], result[12], result[11], result[10], result[9], result[8], result[7], result[6], result[5], result[4], result[3], result[2], result[1], result[0], result[13]);
  not not_2 (Zero, or_2_out);

  // Notes on the sheet:
  //   ALU ASSEMBLED
  //   Shift = 00, Compare = 01, Arithmetic = 10, Logical = 11
endmodule

module Logical (
  input  [31:0] B,
  input  [31:0] A,
  input  [1:0] Operation,
  output [31:0] result
);

  wire [31:0] and_1_out, nor_1_out, or_1_out, xor_1_out;

  assign and_1_out = A & B;  // AND_Gate and_1, 32 bits wide
  assign or_1_out = A | B;  // OR_Gate or_1, 32 bits wide
  assign nor_1_out = ~(A | B);  // NOR_Gate nor_1, 32 bits wide
  assign xor_1_out = A ^ B;  // XOR_Gate xor_1, 32 bits wide
  Multiplexer #(.select(2), .width(32), .enable("false")) multiplexer_1 (
    .in0(and_1_out), .in1(or_1_out), .in2(nor_1_out), .in3(xor_1_out), .out(result), .sel(Operation));

  // Notes on the sheet:
  //   LOGICAL UNIT
  //   AND = 00, OR = 01, NOR = 10, XOR = 11
  //   AND
  //   OR
  //   NOR
  //   XOR
endmodule

module RippleCarryAdder (
  input  [31:0] B,
  input  ADD_SUB,
  input  [31:0] A,
  output [31:0] final_output,
  output Overflow,
  output Carry_out
);

  wire fulladder_1_cout, fulladder_2_cout, fulladder_3_cout, fulladder_4_cout, fulladder_5_cout,
       fulladder_6_cout, fulladder_7_cout, fulladder_8_cout, fulladder_9_cout, fulladder_10_cout,
       fulladder_11_cout, fulladder_12_cout, fulladder_13_cout, fulladder_14_cout, fulladder_15_cout,
       fulladder_16_cout, fulladder_17_cout, fulladder_18_cout, fulladder_19_cout, fulladder_20_cout,
       fulladder_21_cout, fulladder_22_cout, fulladder_23_cout, fulladder_24_cout, fulladder_25_cout,
       fulladder_26_cout, fulladder_27_cout, fulladder_28_cout, fulladder_29_cout, fulladder_30_cout,
       fulladder_31_cout;
  wire [7:0] ByteB0, ByteB1, ByteB2, ByteB3;
  wire [31:0] bit_extender_1_out;

  FullAdder fulladder_1 (.Cout(fulladder_1_cout), .S(final_output[0]), .A(A[0]), .B(ByteB0[0]), .Cin(ADD_SUB));
  FullAdder fulladder_2 (
    .Cout(fulladder_2_cout), .S(final_output[8]), .A(A[8]), .B(ByteB1[0]), .Cin(fulladder_29_cout));
  FullAdder fulladder_3 (
    .Cout(fulladder_3_cout), .S(final_output[16]), .A(A[16]), .B(ByteB2[0]), .Cin(fulladder_30_cout));
  FullAdder fulladder_4 (
    .Cout(fulladder_4_cout), .S(final_output[24]), .A(A[24]), .B(ByteB3[0]), .Cin(fulladder_31_cout));
  FullAdder fulladder_5 (.Cout(fulladder_5_cout), .S(final_output[9]), .A(A[9]), .B(ByteB1[1]), .Cin(fulladder_2_cout));
  FullAdder fulladder_6 (
    .Cout(fulladder_6_cout), .S(final_output[17]), .A(A[17]), .B(ByteB2[1]), .Cin(fulladder_3_cout));
  FullAdder fulladder_7 (.Cout(fulladder_7_cout), .S(final_output[1]), .A(A[1]), .B(ByteB0[1]), .Cin(fulladder_1_cout));
  FullAdder fulladder_8 (
    .Cout(fulladder_8_cout), .S(final_output[25]), .A(A[25]), .B(ByteB3[1]), .Cin(fulladder_4_cout));
  FullAdder fulladder_9 (.Cout(fulladder_9_cout), .S(final_output[2]), .A(A[2]), .B(ByteB0[2]), .Cin(fulladder_7_cout));
  FullAdder fulladder_10 (
    .Cout(fulladder_10_cout), .S(final_output[10]), .A(A[10]), .B(ByteB1[2]), .Cin(fulladder_5_cout));
  FullAdder fulladder_11 (
    .Cout(fulladder_11_cout), .S(final_output[18]), .A(A[18]), .B(ByteB2[2]), .Cin(fulladder_6_cout));
  FullAdder fulladder_12 (
    .Cout(fulladder_12_cout), .S(final_output[26]), .A(A[26]), .B(ByteB3[2]), .Cin(fulladder_8_cout));
  FullAdder fulladder_13 (
    .Cout(fulladder_13_cout), .S(final_output[3]), .A(A[3]), .B(ByteB0[3]), .Cin(fulladder_9_cout));
  FullAdder fulladder_14 (
    .Cout(fulladder_14_cout), .S(final_output[11]), .A(A[11]), .B(ByteB1[3]), .Cin(fulladder_10_cout));
  FullAdder fulladder_15 (
    .Cout(fulladder_15_cout), .S(final_output[19]), .A(A[19]), .B(ByteB2[3]), .Cin(fulladder_11_cout));
  FullAdder fulladder_16 (
    .Cout(fulladder_16_cout), .S(final_output[27]), .A(A[27]), .B(ByteB3[3]), .Cin(fulladder_12_cout));
  FullAdder fulladder_17 (
    .Cout(fulladder_17_cout), .S(final_output[4]), .A(A[4]), .B(ByteB0[4]), .Cin(fulladder_13_cout));
  FullAdder fulladder_18 (
    .Cout(fulladder_18_cout), .S(final_output[12]), .A(A[12]), .B(ByteB1[4]), .Cin(fulladder_14_cout));
  FullAdder fulladder_19 (
    .Cout(fulladder_19_cout), .S(final_output[20]), .A(A[20]), .B(ByteB2[4]), .Cin(fulladder_15_cout));
  FullAdder fulladder_20 (
    .Cout(fulladder_20_cout), .S(final_output[28]), .A(A[28]), .B(ByteB3[4]), .Cin(fulladder_16_cout));
  FullAdder fulladder_21 (
    .Cout(fulladder_21_cout), .S(final_output[13]), .A(A[13]), .B(ByteB1[5]), .Cin(fulladder_18_cout));
  FullAdder fulladder_22 (
    .Cout(fulladder_22_cout), .S(final_output[21]), .A(A[21]), .B(ByteB2[5]), .Cin(fulladder_19_cout));
  assign bit_extender_1_out = {{31{ADD_SUB}}, ADD_SUB};  // Bit_Extender bit_extender_1
  FullAdder fulladder_23 (
    .Cout(fulladder_23_cout), .S(final_output[5]), .A(A[5]), .B(ByteB0[5]), .Cin(fulladder_17_cout));
  FullAdder fulladder_24 (
    .Cout(fulladder_24_cout), .S(final_output[29]), .A(A[29]), .B(ByteB3[5]), .Cin(fulladder_20_cout));
  FullAdder fulladder_25 (
    .Cout(fulladder_25_cout), .S(final_output[6]), .A(A[6]), .B(ByteB0[6]), .Cin(fulladder_23_cout));
  FullAdder fulladder_26 (
    .Cout(fulladder_26_cout), .S(final_output[14]), .A(A[14]), .B(ByteB1[6]), .Cin(fulladder_21_cout));
  FullAdder fulladder_27 (
    .Cout(fulladder_27_cout), .S(final_output[22]), .A(A[22]), .B(ByteB2[6]), .Cin(fulladder_22_cout));
  FullAdder fulladder_28 (
    .Cout(fulladder_28_cout), .S(final_output[30]), .A(A[30]), .B(ByteB3[6]), .Cin(fulladder_24_cout));
  assign {ByteB3, ByteB2, ByteB1, ByteB0} = B ^ bit_extender_1_out;  // XOR_Gate xor_1, 32 bits wide
  FullAdder fulladder_29 (
    .Cout(fulladder_29_cout), .S(final_output[7]), .A(A[7]), .B(ByteB0[7]), .Cin(fulladder_25_cout));
  FullAdder fulladder_30 (
    .Cout(fulladder_30_cout), .S(final_output[15]), .A(A[15]), .B(ByteB1[7]), .Cin(fulladder_26_cout));
  FullAdder fulladder_31 (
    .Cout(fulladder_31_cout), .S(final_output[23]), .A(A[23]), .B(ByteB2[7]), .Cin(fulladder_27_cout));
  FullAdder fulladder_32 (.Cout(Carry_out), .S(final_output[31]), .A(A[31]), .B(ByteB3[7]), .Cin(fulladder_28_cout));
  xor xor_2 (Overflow, fulladder_28_cout, Carry_out);

  // Other names for the same wires on the sheet: ByteA0[7:0] = A[7:0]; ByteA1[7:0] = A[15:8]; ByteA2[7:0] = A[23:16];
  //   ByteA3[7:0] = A[31:24]; Cout = Carry_out; S0[7:0] = final_output[7:0]; S1[7:0] = final_output[15:8];
  //   S2[7:0] = final_output[23:16]; S3[7:0] = final_output[31:24]

  // Notes on the sheet:
  //   ARITHEMTIC UNIT
endmodule

module FullAdder (
  input  Cin,
  input  B,
  input  A,
  output S,
  output Cout
);

  wire and_1_out, and_2_out, xor_1_out;

  xor xor_1 (xor_1_out, A, B);
  and and_1 (and_1_out, xor_1_out, Cin);
  and and_2 (and_2_out, A, B);
  xor xor_2 (S, xor_1_out, Cin);
  or or_1 (Cout, and_1_out, and_2_out);

  // Notes on the sheet:
  //   1-BIT ADDER
endmodule

module Shifts (
  input  [31:0] Z,
  input  [4:0] ShiftAmount,
  input  [1:0] ShiftOp,
  output [31:0] out_4
);

  wire bit1, bit2, bit4, bit8, bit16, decoder_1_out1;
  wire [31:0] bit_extender_1_out, result_high, S1_high, S1_low, S2_high, S2_low, S3_high, S3_low, S4_high,
       S4_low, S5_high, S5_low;

  assign bit_extender_1_out = {{31{Z[31]}}, Z[31]};  // Bit_Extender bit_extender_1
  Multiplexer #(.select(2), .width(32), .enable("false")) multiplexer_1 (
    .in0(Z), .in1({Z[0], {31{1'b0}}}), .in2(Z), .in3(Z), .out(S1_low), .sel(ShiftOp));
  Multiplexer #(.select(2), .width(32), .enable("false")) multiplexer_2 (
    .in0({1'b0, Z[30:0]}), .in1({1'b0, Z[31:1]}), .in2({32{1'b0}}), .in3(bit_extender_1_out), .out(S1_high),
    .sel(ShiftOp));
  Multiplexer #(.width(32), .enable("false")) multiplexer_3 (
    .in0(S1_low), .in1({S1_high[15:0], S1_low[31:16]}), .out(S2_low), .sel(bit16));
  Multiplexer #(.width(32), .enable("false")) multiplexer_4 (
    .in0(S1_high), .in1({{16{1'b0}}, S1_high[31:16]}), .out(S2_high), .sel(bit16));
  Multiplexer #(.width(32), .enable("false")) multiplexer_5 (
    .in0(S2_low), .in1({S2_high[7:0], S2_low[31:8]}), .out(S3_low), .sel(bit8));
  Multiplexer #(.width(32), .enable("false")) multiplexer_6 (
    .in0(S2_high), .in1({{8{1'b0}}, S2_high[31:8]}), .out(S3_high), .sel(bit8));
  Multiplexer #(.width(32), .enable("false")) multiplexer_7 (
    .in0(S5_low), .in1({S5_high[0], S5_low[31:1]}), .out(out_4), .sel(bit1));
  Multiplexer #(.width(32), .enable("false")) multiplexer_8 (
    .in0(S5_high), .in1({1'b0, S5_high[31:1]}), .out(result_high), .sel(bit1));
  Decoder #(.select(2), .enable("false")) decoder_1 (.out1(decoder_1_out1), .sel(ShiftOp));  // open: out0, out2, out3
  xor xor_1 (bit1, ShiftAmount[0], decoder_1_out1);
  xor xor_2 (bit2, ShiftAmount[1], decoder_1_out1);
  xor xor_3 (bit4, ShiftAmount[2], decoder_1_out1);
  xor xor_4 (bit8, ShiftAmount[3], decoder_1_out1);
  xor xor_5 (bit16, ShiftAmount[4], decoder_1_out1);
  Multiplexer #(.width(32), .enable("false")) multiplexer_9 (
    .in0(S3_low), .in1({S3_high[3:0], S3_low[31:4]}), .out(S4_low), .sel(bit4));
  Multiplexer #(.width(32), .enable("false")) multiplexer_10 (
    .in0(S3_high), .in1({4'b0000, S3_high[31:4]}), .out(S4_high), .sel(bit4));
  Multiplexer #(.width(32), .enable("false")) multiplexer_11 (
    .in0(S4_low), .in1({S4_high[1:0], S4_low[31:2]}), .out(S5_low), .sel(bit2));
  Multiplexer #(.width(32), .enable("false")) multiplexer_12 (
    .in0(S4_high), .in1({2'b00, S4_high[31:2]}), .out(S5_high), .sel(bit2));

  // Other names for the same wires on the sheet: result_low[31:0] = out_4

  // Notes on the sheet:
  //   SHIFTER
  //   ROR = 00, SLL = 01, SRL = 10, SRA = 11
endmodule

module Compare (
  input  Sign,
  input  overflow,
  input  carry_out,
  input  isUnsigned,
  output [31:0] out_5
);

  wire multiplexer_1_out, not_1_out, xor_1_out;

  not not_1 (not_1_out, carry_out);
  xor xor_1 (xor_1_out, Sign, overflow);
  Multiplexer #(.enable("false")) multiplexer_1 (
    .in0(xor_1_out), .in1(not_1_out), .out(multiplexer_1_out), .sel(isUnsigned));
  assign out_5 = {{31{1'b0}}, multiplexer_1_out};  // Bit_Extender bit_extender_1

  // Notes on the sheet:
  //   COMPARATOR
endmodule
