// Logisim project Processor.circ as structural Verilog: 17 circuits, main circuit main
module main (
  input  in_1
);

  wire ALUsrc, Branch, branchlogic_1_pc_src, clk, final_alu_1_zero, Jump, MemRead, MemWrite, RegWrite;
  wire [1:0] maincontrol_1_immsel, WBSel;
  wire [2:0] func3;
  wire [6:0] func7, opcode;
  wire [7:0] aluctrl_1_aluctrl;
  wire [24:7] instructionmemory_1_instructions;
  wire [31:0] adder_2_out, controlled_buffer_1_out, data_memory_1_read_data, final_alu_1_result, imm,
       multiplexer_1_out, multiplexer_2_out, multiplexer_3_out, PC4, PC_q, register_file_1_rs1_data,
       register_file_1_rs2_data;

  Register #(.width(32)) PC (.D(multiplexer_1_out), .en(1'b1), .clk(clk), .Q(PC_q), .clr(in_1));
  Adder #(.width(32)) adder_1 (.a(PC_q), .b(32'h4), .out(PC4));  // open: cin, cout
  InstructionMemory instructionmemory_1 (
    .Address(PC_q),
    .Instructions({func7, instructionmemory_1_instructions[24:15], func3, instructionmemory_1_instructions[11:7], opcode}));
  Clock clock_1 (.out(clk));
  Adder #(.width(32)) adder_2 (.a(PC_q), .b(imm), .out(adder_2_out));  // open: cin, cout
  Register_File register_file_1 (
    .reg_write_en(RegWrite), .clk(clk), .rd_data_in(multiplexer_3_out),
    .rd_addr(instructionmemory_1_instructions[11:7]), .rs1_addr(instructionmemory_1_instructions[19:15]),
    .rs2_addr(instructionmemory_1_instructions[24:20]), .rs1_data(register_file_1_rs1_data),
    .rs2_data(register_file_1_rs2_data));
  Multiplexer #(.width(32), .enable("false")) multiplexer_1 (
    .in0(PC4), .in1(adder_2_out), .out(multiplexer_1_out), .sel(branchlogic_1_pc_src));
  Multiplexer #(.width(32), .enable("false")) multiplexer_2 (
    .in0(register_file_1_rs2_data), .in1(imm), .out(multiplexer_2_out), .sel(ALUsrc));
  ALUCtrl aluctrl_1 (.func3(func3), .func7(func7), .opcode(opcode), .ALUCtrl(aluctrl_1_aluctrl));
  immgen immgen_1 (
    .instructions({func7, instructionmemory_1_instructions[24:15], func3, instructionmemory_1_instructions[11:7], opcode}),
    .immsel(maincontrol_1_immsel), .out_3(imm));
  final_ALU final_alu_1 (
    .A(register_file_1_rs1_data), .B(multiplexer_2_out), .ALUCtrl(aluctrl_1_aluctrl),
    .result(final_alu_1_result), .zero(final_alu_1_zero));  // open: overflow, carryout
  branchLogic branchlogic_1 (
    .func3(func3), .branch(Branch), .jump(Jump), .zeroFlag(final_alu_1_zero), .PC_src(branchlogic_1_pc_src));
  MainControl maincontrol_1 (
    .opcode(opcode), .RegWrite(RegWrite), .ALUSRC(ALUsrc), .MEMREAD(MemRead), .MEMWrite(MemWrite),
    .Branch(Branch), .Jump(Jump), .WBSel(WBSel), .ImmSel(maincontrol_1_immsel));
  Data_memory data_memory_1 (
    .mem_write_en(MemWrite), .access_size(func3[1:0]), .clk(clk), .addr(final_alu_1_result),
    .write_data(register_file_1_rs2_data), .read_data(data_memory_1_read_data));
  assign controlled_buffer_1_out = MemRead ? data_memory_1_read_data : 32'bz;  // Controlled_Buffer controlled_buffer_1
  Multiplexer #(.select(2), .width(32), .enable("false")) multiplexer_3 (
    .in0(final_alu_1_result), .in1(controlled_buffer_1_out), .in2(PC4), .out(multiplexer_3_out), .sel(WBSel));  // open: in3
endmodule

module register_and_data_test (
  input  mem_write_en,
  input  reg_write_en,
  input  [1:0] access_size,
  input  [31:0] rd_data_in,
  input  [4:0] rd_addr,
  input  [31:0] addr,
  input  [4:0] rs1_addr,
  input  [4:0] rs2_addr,
  input  [31:0] write_data,
  output [31:0] rs1_data,
  output [31:0] read_data,
  output [31:0] rs2_data
);

  wire clk;

  Register_File register_file_1 (
    .reg_write_en(reg_write_en), .clk(clk), .rd_data_in(rd_data_in), .rd_addr(rd_addr), .rs1_addr(rs1_addr),
    .rs2_addr(rs2_addr), .rs1_data(rs1_data), .rs2_data(rs2_data));
  Clock u_clk (.out(clk));
  Data_memory data_memory_1 (
    .mem_write_en(mem_write_en), .access_size(access_size), .clk(clk), .addr(addr), .write_data(write_data),
    .read_data(read_data));

  // Notes on the sheet:
  //   LAB 03
  //   Name: Sadiksha Lamsal
  //   Date: 4/28/2026
endmodule

module Data_memory (
  input  mem_write_en,
  input  [1:0] access_size,
  input  clk,
  input  [31:0] addr,
  input  [31:0] write_data,
  output [31:0] read_data
);

  wire and_1_out, and_2_out, comparator_1_eq, comparator_2_eq, decoder_1_out0, decoder_1_out1,
       decoder_1_out2, decoder_1_out3, not_1_out, not_2_out, not_3_out, not_4_out, not_5_out, or_1_out,
       or_2_out, or_3_out, or_4_out, W0, W1, W2, W3;
  wire [7:0] D0, D1, D2, D3, multiplexer_2_out;
  wire [15:0] multiplexer_1_out;
  wire [31:0] bit_extender_2_out, halfword;

  RAM #(.addrWidth(24), .databus("bibus")) ram_1 (
    .addr(addr[25:2]), .we(W0), .oe(1'b1), .clk(not_1_out), .din(write_data[7:0]), .dout(D0));
  not not_1 (not_1_out, clk);
  Multiplexer #(.width(16), .enable("false")) multiplexer_1 (
    .in0({D1, D0}), .in1({D3, D2}), .out(multiplexer_1_out), .sel(addr[1]));
  assign halfword = {{16{multiplexer_1_out[15]}}, multiplexer_1_out};  // Bit_Extender bit_extender_1
  // Probe on D0
  RAM #(.addrWidth(24), .databus("bibus")) ram_2 (
    .addr(addr[25:2]), .we(W1), .oe(1'b1), .clk(not_2_out), .din(write_data[15:8]), .dout(D1));
  not not_2 (not_2_out, clk);
  Comparator #(.width(2)) comparator_1 (.a(access_size), .b(2'b01), .eq(comparator_1_eq));  // open: gt, lt
  Decoder #(.select(2)) decoder_1 (
    .out0(decoder_1_out0), .out1(decoder_1_out1), .out2(decoder_1_out2), .out3(decoder_1_out3),
    .sel(addr[1:0]));  // open: en
  not not_3 (not_3_out, addr[1]);
  Comparator #(.width(2)) comparator_2 (.a(access_size), .b(2'b10), .eq(comparator_2_eq));  // open: gt, lt
  // Probe on D1
  and and_1 (and_1_out, comparator_1_eq, not_3_out);
  and and_2 (and_2_out, comparator_1_eq, addr[1]);
  RAM #(.addrWidth(24), .databus("bibus")) ram_3 (
    .addr(addr[25:2]), .we(W2), .oe(1'b1), .clk(not_4_out), .din(write_data[23:16]), .dout(D2));
  not not_4 (not_4_out, clk);
  or or_1 (or_1_out, decoder_1_out0, and_1_out, comparator_2_eq);
  or or_2 (or_2_out, decoder_1_out1, and_1_out, comparator_2_eq);
  or or_3 (or_3_out, decoder_1_out2, and_2_out, comparator_2_eq);
  or or_4 (or_4_out, decoder_1_out3, and_2_out, comparator_2_eq);
  and and_3 (W0, or_1_out, mem_write_en);
  and and_4 (W1, or_2_out, mem_write_en);
  and and_5 (W2, or_3_out, mem_write_en);
  and and_6 (W3, or_4_out, mem_write_en);
  Multiplexer #(.select(2), .width(8), .enable("false")) multiplexer_2 (
    .in0(D0), .in1(D1), .in2(D2), .in3(D3), .out(multiplexer_2_out), .sel(addr[1:0]));
  // Probe on D2
  RAM #(.addrWidth(24), .databus("bibus")) ram_4 (
    .addr(addr[25:2]), .we(W3), .oe(1'b1), .clk(not_5_out), .din(write_data[31:24]), .dout(D3));
  not not_5 (not_5_out, clk);
  assign bit_extender_2_out = {{24{multiplexer_2_out[7]}}, multiplexer_2_out};  // Bit_Extender bit_extender_2
  Multiplexer #(.select(2), .width(32), .enable("false")) multiplexer_3 (
    .in0(bit_extender_2_out), .in1(halfword), .in2({D3, D2, D1, D0}), .out(read_data), .sel(access_size));  // open: in3
  // Probe on D3

  // Other names for the same wires on the sheet: addr01[1:0] = addr[1:0]; raw_word[31:0] = {D3, D2, D1, D0};
  //   WD0[7:0] = write_data[7:0]; WD1[7:0] = write_data[15:8]; WD2[7:0] = write_data[23:16];
  //   WD3[7:0] = write_data[31:24]

  // Notes on the sheet:
  //   DATA MEMORY
endmodule

module Register_File (
  input  reg_write_en,
  input  clk,
  input  [31:0] rd_data_in,
  input  [4:0] rd_addr,
  input  [4:0] rs1_addr,
  input  [4:0] rs2_addr,
  output [31:0] rs1_data,
  output [31:0] rs2_data
);

  wire and_1_out, and_2_out, and_3_out, and_4_out, and_5_out, and_6_out, and_7_out, and_8_out, and_9_out,
       and_10_out, and_11_out, and_12_out, and_13_out, and_14_out, and_15_out, and_16_out, and_17_out,
       and_18_out, and_19_out, and_20_out, and_21_out, and_22_out, and_23_out, and_24_out, and_25_out,
       and_26_out, and_27_out, and_28_out, and_29_out, and_30_out, and_31_out, s1, s2, s3, s4, s5, s6, s7,
       s8, s9, s10, s11, s12, s13, s14, s15, s16, s17, s18, s19, s20, s21, s22, s23, s24, s25, s26, s27, s28,
       s29, s30, s31;
  wire [31:0] r1, r2, r3, r4, r5, r6, r7, r8, r9, r10, r11, r12, r13, r14, r15, r16, r17, r18, r19, r20, r21,
       r22, r23, r24, r25, r26, r27, r28, r29, r30, r31;

  Decoder #(.select(5)) decoder_1 (
    .out1(s1), .out2(s2), .out3(s3), .out4(s4), .out5(s5), .out6(s6), .out7(s7), .out8(s8), .out9(s9),
    .out10(s10), .out11(s11), .out12(s12), .out13(s13), .out14(s14), .out15(s15), .out16(s16), .out17(s17),
    .out18(s18), .out19(s19), .out20(s20), .out21(s21), .out22(s22), .out23(s23), .out24(s24), .out25(s25),
    .out26(s26), .out27(s27), .out28(s28), .out29(s29), .out30(s30), .out31(s31), .sel(rd_addr));  // open: out0, en
  and and_1 (and_1_out, reg_write_en, s1);
  and and_2 (and_2_out, reg_write_en, s2);
  and and_3 (and_3_out, reg_write_en, s3);
  and and_4 (and_4_out, reg_write_en, s4);
  and and_5 (and_5_out, reg_write_en, s5);
  and and_6 (and_6_out, reg_write_en, s6);
  and and_7 (and_7_out, reg_write_en, s7);
  Register #(.width(32)) x1 (.D(rd_data_in), .en(and_1_out), .clk(clk), .Q(r1));  // open: clr
  Register #(.width(32)) x2 (.D(rd_data_in), .en(and_2_out), .clk(clk), .Q(r2));  // open: clr
  Register #(.width(32)) x3 (.D(rd_data_in), .en(and_3_out), .clk(clk), .Q(r3));  // open: clr
  Register #(.width(32)) x4 (.D(rd_data_in), .en(and_4_out), .clk(clk), .Q(r4));  // open: clr
  Register #(.width(32)) x5 (.D(rd_data_in), .en(and_5_out), .clk(clk), .Q(r5));  // open: clr
  Register #(.width(32)) x6 (.D(rd_data_in), .en(and_6_out), .clk(clk), .Q(r6));  // open: clr
  Register #(.width(32)) x7 (.D(rd_data_in), .en(and_7_out), .clk(clk), .Q(r7));  // open: clr
  Multiplexer #(.select(5), .width(32), .enable("false")) multiplexer_1 (
    .in0({32{1'b0}}), .in1(r1), .in2(r2), .in3(r3), .in4(r4), .in5(r5), .in6(r6), .in7(r7), .in8(r8),
    .in9(r9), .in10(r10), .in11(r11), .in12(r12), .in13(r13), .in14(r14), .in15(r15), .in16(r16), .in17(r17),
    .in18(r18), .in19(r19), .in20(r20), .in21(r21), .in22(r22), .in23(r23), .in24(r24), .in25(r25),
    .in26(r26), .in27(r27), .in28(r28), .in29(r29), .in30(r30), .in31(r31), .out(rs1_data), .sel(rs1_addr));
  Register #(.width(32)) x8 (.D(rd_data_in), .en(and_8_out), .clk(clk), .Q(r8));  // open: clr
  and and_8 (and_8_out, reg_write_en, s8);
  Register #(.width(32)) x9 (.D(rd_data_in), .en(and_9_out), .clk(clk), .Q(r9));  // open: clr
  and and_9 (and_9_out, reg_write_en, s9);
  and and_10 (and_10_out, reg_write_en, s10);
  Register #(.width(32)) x11 (.D(rd_data_in), .en(and_11_out), .clk(clk), .Q(r11));  // open: clr
  and and_11 (and_11_out, reg_write_en, s11);
  Register #(.width(32)) x12 (.D(rd_data_in), .en(and_12_out), .clk(clk), .Q(r12));  // open: clr
  and and_12 (and_12_out, reg_write_en, s12);
  and and_13 (and_13_out, reg_write_en, s13);
  Register #(.width(32)) x14 (.D(rd_data_in), .en(and_14_out), .clk(clk), .Q(r14));  // open: clr
  and and_14 (and_14_out, reg_write_en, s14);
  and and_15 (and_15_out, reg_write_en, s15);
  Register #(.width(32)) x10 (.D(rd_data_in), .en(and_10_out), .clk(clk), .Q(r10));  // open: clr
  Register #(.width(32)) x13 (.D(rd_data_in), .en(and_13_out), .clk(clk), .Q(r13));  // open: clr
  Register #(.width(32)) x15 (.D(rd_data_in), .en(and_15_out), .clk(clk), .Q(r15));  // open: clr
  Multiplexer #(.select(5), .width(32), .enable("false")) multiplexer_2 (
    .in0({32{1'b0}}), .in1(r1), .in2(r2), .in3(r3), .in4(r4), .in5(r5), .in6(r6), .in7(r7), .in8(r8),
    .in9(r9), .in10(r10), .in11(r11), .in12(r12), .in13(r13), .in14(r14), .in15(r15), .in16(r16), .in17(r17),
    .in18(r18), .in19(r19), .in20(r20), .in21(r21), .in22(r22), .in23(r23), .in24(r24), .in25(r25),
    .in26(r26), .in27(r27), .in28(r28), .in29(r29), .in30(r30), .in31(r31), .out(rs2_data), .sel(rs2_addr));
  and and_16 (and_16_out, reg_write_en, s16);
  and and_17 (and_17_out, reg_write_en, s17);
  and and_18 (and_18_out, reg_write_en, s19);
  and and_19 (and_19_out, reg_write_en, s22);
  Register #(.width(32)) x16 (.D(rd_data_in), .en(and_16_out), .clk(clk), .Q(r16));  // open: clr
  Register #(.width(32)) x17 (.D(rd_data_in), .en(and_17_out), .clk(clk), .Q(r17));  // open: clr
  Register #(.width(32)) x18 (.D(rd_data_in), .en(and_20_out), .clk(clk), .Q(r18));  // open: clr
  and and_20 (and_20_out, reg_write_en, s18);
  Register #(.width(32)) x19 (.D(rd_data_in), .en(and_18_out), .clk(clk), .Q(r19));  // open: clr
  Register #(.width(32)) x20 (.D(rd_data_in), .en(and_21_out), .clk(clk), .Q(r20));  // open: clr
  and and_21 (and_21_out, reg_write_en, s20);
  Register #(.width(32)) x21 (.D(rd_data_in), .en(and_22_out), .clk(clk), .Q(r21));  // open: clr
  and and_22 (and_22_out, reg_write_en, s21);
  Register #(.width(32)) x22 (.D(rd_data_in), .en(and_19_out), .clk(clk), .Q(r22));  // open: clr
  Register #(.width(32)) x23 (.D(rd_data_in), .en(and_23_out), .clk(clk), .Q(r23));  // open: clr
  and and_23 (and_23_out, reg_write_en, s23);
  Register #(.width(32)) x24 (.D(rd_data_in), .en(and_24_out), .clk(clk), .Q(r24));  // open: clr
  and and_24 (and_24_out, reg_write_en, s24);
  Register #(.width(32)) x25 (.D(rd_data_in), .en(and_25_out), .clk(clk), .Q(r25));  // open: clr
  and and_25 (and_25_out, reg_write_en, s25);
  Register #(.width(32)) x26 (.D(rd_data_in), .en(and_26_out), .clk(clk), .Q(r26));  // open: clr
  and and_26 (and_26_out, reg_write_en, s26);
  Register #(.width(32)) x27 (.D(rd_data_in), .en(and_27_out), .clk(clk), .Q(r27));  // open: clr
  and and_27 (and_27_out, reg_write_en, s27);
  Register #(.width(32)) x28 (.D(rd_data_in), .en(and_28_out), .clk(clk), .Q(r28));  // open: clr
  and and_28 (and_28_out, reg_write_en, s28);
  Register #(.width(32)) x29 (.D(rd_data_in), .en(and_29_out), .clk(clk), .Q(r29));  // open: clr
  and and_29 (and_29_out, reg_write_en, s29);
  Register #(.width(32)) x30 (.D(rd_data_in), .en(and_30_out), .clk(clk), .Q(r30));  // open: clr
  and and_30 (and_30_out, reg_write_en, s30);
  Register #(.width(32)) x31 (.D(rd_data_in), .en(and_31_out), .clk(clk), .Q(r31));  // open: clr
  and and_31 (and_31_out, reg_write_en, s31);

  // Notes on the sheet:
  //   REGISTER FILE
endmodule

module ALU_Test (
  output [31:0] result,
  output zero,
  output overflow,
  output carry_out
);

  wire clk;
  wire [3:0] Control_Register_q, Control_ROM_data, Count_q;
  wire [31:0] Register_A_q, Register_B_q, ROM_A_data, ROM_B_data;

  Clock sysclk ();  // open: out
  Counter #(.width(4), .max('hf)) Count (.clk(clk), .Q(Count_q));  // open: clr, load, up, count, D, carry
  Clock u_clk (.out(clk));
  ROM #(.addrWidth(4), .dataWidth(4)) Control_ROM (.addr(Count_q), .data(Control_ROM_data));
  Register #(.width(4)) Control_Register (
    .D(Control_ROM_data), .en(1'b1), .clk(clk), .Q(Control_Register_q));  // open: clr
  ROM #(.addrWidth(4), .dataWidth(32)) ROM_A (.addr(Count_q), .data(ROM_A_data));
  // Probe on Control_Register_q[2]
  // Probe on Register_A_q
  // Probe on Control_Register_q[1:0]
  Register #(.width(32)) Register_A (.D(ROM_A_data), .en(1'b1), .clk(clk), .Q(Register_A_q));  // open: clr
  // Probe on Register_B_q
  ROM #(.addrWidth(4), .dataWidth(32)) ROM_B (.addr(Count_q), .data(ROM_B_data));
  ALU_assembled alu_assembled_1 (
    .A(Register_A_q), .B(Register_B_q), .ShiftOp(Control_Register_q[3:2]),
    .isUnsigned(Control_Register_q[2]), .Add_SUB(Control_Register_q[2]), .LogicalOp(Control_Register_q[3:2]),
    .ALU_Selection(Control_Register_q[1:0]), .result(result), .Zero(zero), .overflow(overflow),
    .carry_out(carry_out));
  Register #(.width(32)) Register_B (.D(ROM_B_data), .en(1'b1), .clk(clk), .Q(Register_B_q));  // open: clr

  // Notes on the sheet:
  //   LAB 02: ALU
  //   Name: Sadiksha Lamsal
  //   Date: 4/19//2026
  //   TEST BENCH
  //   contents of Control_ROM (hex, n*v repeats v):
  //   0 4 8 c 1 2 2 6 3 7 b f
  //   contents of ROM_A (hex, n*v repeats v):
  //   4*aaaaaaa5 2 7fffffff 5 80000000 f0f0f0f0 f0f0f0f0 0 aaaaaaaa
  //   contents of ROM_B (hex, n*v repeats v):
  //   4*4 5 1 3 80000000 f0f0f0f f0f0f0f 0 55555555
endmodule

module final_ALU (
  input  [31:0] A,
  input  [31:0] B,
  input  [7:0] ALUCtrl,
  output [31:0] result,
  output zero,
  output overflow,
  output carryout
);

  ALU_assembled alu_assembled_1 (
    .A(A), .B(B), .ShiftOp(ALUCtrl[3:2]), .isUnsigned(ALUCtrl[7]), .Add_SUB(ALUCtrl[6]),
    .LogicalOp(ALUCtrl[5:4]), .ALU_Selection(ALUCtrl[1:0]), .result(result), .Zero(zero),
    .overflow(overflow), .carry_out(carryout));

  // Notes on the sheet:
  //   ALU CIRCUIT
endmodule

module ALU_assembled (
  input  [31:0] A,
  input  [31:0] B,
  input  [1:0] ShiftOp,
  input  isUnsigned,
  input  Add_SUB,
  input  [1:0] LogicalOp,
  input  [1:0] ALU_Selection,
  output [31:0] result,
  output Zero,
  output overflow,
  output carry_out
);

  wire Comparator, not_1_out, or_1_out, or_2_out;
  wire [31:0] compare_1_out_5, logical_1_result, ripplecarryadder_1_final_output, shifts_1_out_4;

  or or_1 (or_1_out, Comparator, Add_SUB);
  and and_1 (Comparator, ALU_Selection[0], not_1_out);
  not not_1 (not_1_out, ALU_Selection[1]);
  Shifts shifts_1 (.Z(A), .ShiftAmount(B[4:0]), .ShiftOp(ShiftOp), .out_4(shifts_1_out_4));
  RippleCarryAdder ripplecarryadder_1 (
    .B(B), .ADD_SUB(or_1_out), .A(A), .final_output(ripplecarryadder_1_final_output), .Overflow(overflow),
    .Carry_out(carry_out));
  Logical logical_1 (.B(B), .A(A), .Operation(LogicalOp), .result(logical_1_result));
  Compare compare_1 (
    .Sign(ripplecarryadder_1_final_output[31]), .overflow(overflow), .carry_out(carry_out),
    .isUnsigned(isUnsigned), .out_5(compare_1_out_5));
  Multiplexer #(.select(2), .width(32), .enable("false")) multiplexer_1 (
    .in0(shifts_1_out_4), .in1(compare_1_out_5), .in2(ripplecarryadder_1_final_output),
    .in3(logical_1_result), .out(result), .sel(ALU_Selection));
  or or_2 (or_2_out, result[31], result[30], result[29], result[28], result[27], result[26], result[25], result[24], result[23], result[22], result[21], result[20], result[19], result[18], result[17], result[16], result[15], result[14], result[12], result[11], result[10], result[9], result[8], result[7], result[6], result[5], result[4], result[3], result[2], result[1], result[0], result[13]);
  not not_2 (Zero, or_2_out);

  // Notes on the sheet:
  //   ALU ASSEMBLED
  //   Shift = 00, Compare = 01, Arithmetic = 10, Logical = 11
endmodule

module Logical (
  input  [31:0] B,
  input  [31:0] A,
  input  [1:0] Operation,
  output [31:0] result
);

  wire [31:0] and_1_out, nor_1_out, or_1_out, xor_1_out;

  assign and_1_out = A & B;  // AND_Gate and_1, 32 bits wide
  assign or_1_out = A | B;  // OR_Gate or_1, 32 bits wide
  assign nor_1_out = ~(A | B);  // NOR_Gate nor_1, 32 bits wide
  assign xor_1_out = A ^ B;  // XOR_Gate xor_1, 32 bits wide
  Multiplexer #(.select(2), .width(32), .enable("false")) multiplexer_1 (
    .in0(and_1_out), .in1(or_1_out), .in2(nor_1_out), .in3(xor_1_out), .out(result), .sel(Operation));

  // Notes on the sheet:
  //   LOGICAL UNIT
  //   AND = 00, OR = 01, NOR = 10, XOR = 11
  //   AND
  //   OR
  //   NOR
  //   XOR
endmodule

module RippleCarryAdder (
  input  [31:0] B,
  input  ADD_SUB,
  input  [31:0] A,
  output [31:0] final_output,
  output Overflow,
  output Carry_out
);

  wire fulladder_1_cout, fulladder_2_cout, fulladder_3_cout, fulladder_4_cout, fulladder_5_cout,
       fulladder_6_cout, fulladder_7_cout, fulladder_8_cout, fulladder_9_cout, fulladder_10_cout,
       fulladder_11_cout, fulladder_12_cout, fulladder_13_cout, fulladder_14_cout, fulladder_15_cout,
       fulladder_16_cout, fulladder_17_cout, fulladder_18_cout, fulladder_19_cout, fulladder_20_cout,
       fulladder_21_cout, fulladder_22_cout, fulladder_23_cout, fulladder_24_cout, fulladder_25_cout,
       fulladder_26_cout, fulladder_27_cout, fulladder_28_cout, fulladder_29_cout, fulladder_30_cout,
       fulladder_31_cout;
  wire [7:0] ByteB0, ByteB1, ByteB2, ByteB3;
  wire [31:0] bit_extender_1_out;

  FullAdder fulladder_1 (.Cout(fulladder_1_cout), .Cin(ADD_SUB), .S(final_output[0]), .B(ByteB0[0]), .A(A[0]));
  FullAdder fulladder_2 (
    .Cout(fulladder_2_cout), .Cin(fulladder_29_cout), .S(final_output[8]), .B(ByteB1[0]), .A(A[8]));
  FullAdder fulladder_3 (
    .Cout(fulladder_3_cout), .Cin(fulladder_30_cout), .S(final_output[16]), .B(ByteB2[0]), .A(A[16]));
  FullAdder fulladder_4 (
    .Cout(fulladder_4_cout), .Cin(fulladder_31_cout), .S(final_output[24]), .B(ByteB3[0]), .A(A[24]));
  FullAdder fulladder_5 (.Cout(fulladder_5_cout), .Cin(fulladder_2_cout), .S(final_output[9]), .B(ByteB1[1]), .A(A[9]));
  FullAdder fulladder_6 (
    .Cout(fulladder_6_cout), .Cin(fulladder_3_cout), .S(final_output[17]), .B(ByteB2[1]), .A(A[17]));
  FullAdder fulladder_7 (.Cout(fulladder_7_cout), .Cin(fulladder_1_cout), .S(final_output[1]), .B(ByteB0[1]), .A(A[1]));
  FullAdder fulladder_8 (
    .Cout(fulladder_8_cout), .Cin(fulladder_4_cout), .S(final_output[25]), .B(ByteB3[1]), .A(A[25]));
  FullAdder fulladder_9 (.Cout(fulladder_9_cout), .Cin(fulladder_7_cout), .S(final_output[2]), .B(ByteB0[2]), .A(A[2]));
  FullAdder fulladder_10 (
    .Cout(fulladder_10_cout), .Cin(fulladder_5_cout), .S(final_output[10]), .B(ByteB1[2]), .A(A[10]));
  FullAdder fulladder_11 (
    .Cout(fulladder_11_cout), .Cin(fulladder_6_cout), .S(final_output[18]), .B(ByteB2[2]), .A(A[18]));
  FullAdder fulladder_12 (
    .Cout(fulladder_12_cout), .Cin(fulladder_8_cout), .S(final_output[26]), .B(ByteB3[2]), .A(A[26]));
  FullAdder fulladder_13 (
    .Cout(fulladder_13_cout), .Cin(fulladder_9_cout), .S(final_output[3]), .B(ByteB0[3]), .A(A[3]));
  FullAdder fulladder_14 (
    .Cout(fulladder_14_cout), .Cin(fulladder_10_cout), .S(final_output[11]), .B(ByteB1[3]), .A(A[11]));
  FullAdder fulladder_15 (
    .Cout(fulladder_15_cout), .Cin(fulladder_11_cout), .S(final_output[19]), .B(ByteB2[3]), .A(A[19]));
  FullAdder fulladder_16 (
    .Cout(fulladder_16_cout), .Cin(fulladder_12_cout), .S(final_output[27]), .B(ByteB3[3]), .A(A[27]));
  FullAdder fulladder_17 (
    .Cout(fulladder_17_cout), .Cin(fulladder_13_cout), .S(final_output[4]), .B(ByteB0[4]), .A(A[4]));
  FullAdder fulladder_18 (
    .Cout(fulladder_18_cout), .Cin(fulladder_14_cout), .S(final_output[12]), .B(ByteB1[4]), .A(A[12]));
  FullAdder fulladder_19 (
    .Cout(fulladder_19_cout), .Cin(fulladder_15_cout), .S(final_output[20]), .B(ByteB2[4]), .A(A[20]));
  FullAdder fulladder_20 (
    .Cout(fulladder_20_cout), .Cin(fulladder_16_cout), .S(final_output[28]), .B(ByteB3[4]), .A(A[28]));
  FullAdder fulladder_21 (
    .Cout(fulladder_21_cout), .Cin(fulladder_18_cout), .S(final_output[13]), .B(ByteB1[5]), .A(A[13]));
  FullAdder fulladder_22 (
    .Cout(fulladder_22_cout), .Cin(fulladder_19_cout), .S(final_output[21]), .B(ByteB2[5]), .A(A[21]));
  assign bit_extender_1_out = {{31{ADD_SUB}}, ADD_SUB};  // Bit_Extender bit_extender_1
  FullAdder fulladder_23 (
    .Cout(fulladder_23_cout), .Cin(fulladder_17_cout), .S(final_output[5]), .B(ByteB0[5]), .A(A[5]));
  FullAdder fulladder_24 (
    .Cout(fulladder_24_cout), .Cin(fulladder_20_cout), .S(final_output[29]), .B(ByteB3[5]), .A(A[29]));
  FullAdder fulladder_25 (
    .Cout(fulladder_25_cout), .Cin(fulladder_23_cout), .S(final_output[6]), .B(ByteB0[6]), .A(A[6]));
  FullAdder fulladder_26 (
    .Cout(fulladder_26_cout), .Cin(fulladder_21_cout), .S(final_output[14]), .B(ByteB1[6]), .A(A[14]));
  FullAdder fulladder_27 (
    .Cout(fulladder_27_cout), .Cin(fulladder_22_cout), .S(final_output[22]), .B(ByteB2[6]), .A(A[22]));
  FullAdder fulladder_28 (
    .Cout(fulladder_28_cout), .Cin(fulladder_24_cout), .S(final_output[30]), .B(ByteB3[6]), .A(A[30]));
  assign {ByteB3, ByteB2, ByteB1, ByteB0} = B ^ bit_extender_1_out;  // XOR_Gate xor_1, 32 bits wide
  FullAdder fulladder_29 (
    .Cout(fulladder_29_cout), .Cin(fulladder_25_cout), .S(final_output[7]), .B(ByteB0[7]), .A(A[7]));
  FullAdder fulladder_30 (
    .Cout(fulladder_30_cout), .Cin(fulladder_26_cout), .S(final_output[15]), .B(ByteB1[7]), .A(A[15]));
  FullAdder fulladder_31 (
    .Cout(fulladder_31_cout), .Cin(fulladder_27_cout), .S(final_output[23]), .B(ByteB2[7]), .A(A[23]));
  FullAdder fulladder_32 (.Cout(Carry_out), .Cin(fulladder_28_cout), .S(final_output[31]), .B(ByteB3[7]), .A(A[31]));
  xor xor_2 (Overflow, fulladder_28_cout, Carry_out);

  // Other names for the same wires on the sheet: ByteA0[7:0] = A[7:0]; ByteA1[7:0] = A[15:8]; ByteA2[7:0] = A[23:16];
  //   ByteA3[7:0] = A[31:24]; Cout = Carry_out; S0[7:0] = final_output[7:0]; S1[7:0] = final_output[15:8];
  //   S2[7:0] = final_output[23:16]; S3[7:0] = final_output[31:24]

  // Notes on the sheet:
  //   ARITHEMTIC UNIT
endmodule

module FullAdder (
  input  Cin,
  input  B,
  input  A,
  output S,
  output Cout
);

  wire and_1_out, and_2_out, xor_1_out;

  xor xor_1 (xor_1_out, A, B);
  and and_1 (and_1_out, xor_1_out, Cin);
  and and_2 (and_2_out, A, B);
  xor xor_2 (S, xor_1_out, Cin);
  or or_1 (Cout, and_1_out, and_2_out);

  // Notes on the sheet:
  //   1-BIT ADDER
endmodule

module Shifts (
  input  [31:0] Z,
  input  [4:0] ShiftAmount,
  input  [1:0] ShiftOp,
  output [31:0] out_4
);

  wire bit1, bit2, bit4, bit8, bit16, decoder_1_out1;
  wire [31:0] bit_extender_1_out, result_high, S1_high, S1_low, S2_high, S2_low, S3_high, S3_low, S4_high,
       S4_low, S5_high, S5_low;

  assign bit_extender_1_out = {{31{Z[31]}}, Z[31]};  // Bit_Extender bit_extender_1
  Multiplexer #(.select(2), .width(32), .enable("false")) multiplexer_1 (
    .in0(Z), .in1({Z[0], {31{1'b0}}}), .in2(Z), .in3(Z), .out(S1_low), .sel(ShiftOp));
  Multiplexer #(.select(2), .width(32), .enable("false")) multiplexer_2 (
    .in0({1'b0, Z[30:0]}), .in1({1'b0, Z[31:1]}), .in2({32{1'b0}}), .in3(bit_extender_1_out), .out(S1_high),
    .sel(ShiftOp));
  Multiplexer #(.width(32), .enable("false")) multiplexer_3 (
    .in0(S1_low), .in1({S1_high[15:0], S1_low[31:16]}), .out(S2_low), .sel(bit16));
  Multiplexer #(.width(32), .enable("false")) multiplexer_4 (
    .in0(S1_high), .in1({{16{1'b0}}, S1_high[31:16]}), .out(S2_high), .sel(bit16));
  Multiplexer #(.width(32), .enable("false")) multiplexer_5 (
    .in0(S2_low), .in1({S2_high[7:0], S2_low[31:8]}), .out(S3_low), .sel(bit8));
  Multiplexer #(.width(32), .enable("false")) multiplexer_6 (
    .in0(S2_high), .in1({{8{1'b0}}, S2_high[31:8]}), .out(S3_high), .sel(bit8));
  Multiplexer #(.width(32), .enable("false")) multiplexer_7 (
    .in0(S5_low), .in1({S5_high[0], S5_low[31:1]}), .out(out_4), .sel(bit1));
  Multiplexer #(.width(32), .enable("false")) multiplexer_8 (
    .in0(S5_high), .in1({1'b0, S5_high[31:1]}), .out(result_high), .sel(bit1));
  Decoder #(.select(2), .enable("false")) decoder_1 (.out1(decoder_1_out1), .sel(ShiftOp));  // open: out0, out2, out3
  xor xor_1 (bit1, ShiftAmount[0], decoder_1_out1);
  xor xor_2 (bit2, ShiftAmount[1], decoder_1_out1);
  xor xor_3 (bit4, ShiftAmount[2], decoder_1_out1);
  xor xor_4 (bit8, ShiftAmount[3], decoder_1_out1);
  xor xor_5 (bit16, ShiftAmount[4], decoder_1_out1);
  Multiplexer #(.width(32), .enable("false")) multiplexer_9 (
    .in0(S3_low), .in1({S3_high[3:0], S3_low[31:4]}), .out(S4_low), .sel(bit4));
  Multiplexer #(.width(32), .enable("false")) multiplexer_10 (
    .in0(S3_high), .in1({4'b0000, S3_high[31:4]}), .out(S4_high), .sel(bit4));
  Multiplexer #(.width(32), .enable("false")) multiplexer_11 (
    .in0(S4_low), .in1({S4_high[1:0], S4_low[31:2]}), .out(S5_low), .sel(bit2));
  Multiplexer #(.width(32), .enable("false")) multiplexer_12 (
    .in0(S4_high), .in1({2'b00, S4_high[31:2]}), .out(S5_high), .sel(bit2));

  // Other names for the same wires on the sheet: result_low[31:0] = out_4

  // Notes on the sheet:
  //   SHIFTER
  //   ROR = 00, SLL = 01, SRL = 10, SRA = 11
endmodule

module Compare (
  input  Sign,
  input  overflow,
  input  carry_out,
  input  isUnsigned,
  output [31:0] out_5
);

  wire multiplexer_1_out, not_1_out, xor_1_out;

  not not_1 (not_1_out, carry_out);
  xor xor_1 (xor_1_out, Sign, overflow);
  Multiplexer #(.enable("false")) multiplexer_1 (
    .in0(xor_1_out), .in1(not_1_out), .out(multiplexer_1_out), .sel(isUnsigned));
  assign out_5 = {{31{1'b0}}, multiplexer_1_out};  // Bit_Extender bit_extender_1

  // Notes on the sheet:
  //   COMPARATOR
endmodule

module immgen (
  input  [31:0] instructions,
  input  [1:0] immsel,
  output [31:0] out_3
);

  wire [31:0] B_IMM, I_IMM, J_IMM, S_IMM;

  assign S_IMM = {{20{instructions[31]}}, {instructions[31:25], instructions[11:7]}};  // Bit_Extender bit_extender_1
  assign I_IMM = {{20{instructions[31]}}, instructions[31:20]};  // Bit_Extender bit_extender_2
  assign B_IMM = {{19{instructions[31]}}, {instructions[31], instructions[7], instructions[30:25], instructions[11:8], 1'b0}};  // Bit_Extender bit_extender_3
  assign J_IMM = {{11{instructions[31]}}, {instructions[31], instructions[19:12], instructions[20], instructions[30:21], 1'b0}};  // Bit_Extender bit_extender_4
  Multiplexer #(.select(2), .width(32), .enable("false")) multiplexer_1 (
    .in0(I_IMM), .in1(S_IMM), .in2(B_IMM), .in3(J_IMM), .out(out_3), .sel(immsel));

  // Other names for the same wires on the sheet: inst2031[11:0] = instructions[31:20];
  //   inst2124[3:0] = instructions[24:21]; inst2530[5:0] = instructions[30:25]; inst20 = instructions[20];
  //   inst1219[7:0] = instructions[19:12]; inst31 = instructions[31]; inst811[3:0] = instructions[11:8];
  //   inst7 = instructions[7]; inst06[6:0] = instructions[6:0]
endmodule

module MainControl (
  input  [6:0] opcode,
  output RegWrite,
  output ALUSRC,
  output MEMREAD,
  output MEMWrite,
  output Branch,
  output Jump,
  output [1:0] WBSel,
  output [1:0] ImmSel
);

  wire IsIType, IsRType, not_1_out, not_2_out, not_3_out, not_4_out, not_5_out, not_6_out, not_7_out,
       not_8_out, not_9_out, not_10_out, not_11_out, not_12_out, not_13_out, not_14_out, not_15_out,
       not_16_out, not_17_out, not_18_out, not_19_out, not_20_out;

  not not_1 (not_1_out, opcode[2]);
  not not_2 (not_2_out, opcode[3]);
  not not_3 (not_3_out, opcode[6]);
  not not_4 (not_4_out, opcode[2]);
  not not_5 (not_5_out, opcode[3]);
  not not_6 (not_6_out, opcode[5]);
  not not_7 (not_7_out, opcode[6]);
  not not_8 (not_8_out, opcode[2]);
  not not_9 (not_9_out, opcode[3]);
  not not_10 (not_10_out, opcode[4]);
  not not_11 (not_11_out, opcode[5]);
  not not_12 (not_12_out, opcode[6]);
  not not_13 (not_13_out, opcode[2]);
  not not_14 (not_14_out, opcode[3]);
  not not_15 (not_15_out, opcode[4]);
  not not_16 (not_16_out, opcode[4]);
  not not_17 (not_17_out, opcode[4]);
  not not_18 (not_18_out, opcode[6]);
  not not_19 (not_19_out, opcode[2]);
  not not_20 (not_20_out, opcode[3]);
  and and_1 (IsRType, opcode[0], opcode[1], not_1_out, not_2_out, opcode[4], opcode[5], not_3_out);
  and and_2 (IsIType, opcode[0], opcode[1], not_4_out, not_5_out, opcode[4], not_6_out, not_7_out);
  and and_3 (MEMREAD, opcode[0], opcode[1], not_8_out, not_9_out, not_10_out, not_11_out, not_12_out);
  and and_4 (MEMWrite, opcode[0], opcode[1], not_13_out, not_14_out, not_15_out, opcode[5], not_18_out);
  and and_5 (Branch, opcode[0], opcode[1], not_19_out, not_20_out, not_16_out, opcode[5], opcode[6]);
  and and_6 (Jump, opcode[0], opcode[1], opcode[2], opcode[3], not_17_out, opcode[5], opcode[6]);
  or or_1 (ImmSel[0], Jump, MEMWrite);
  or or_2 (ImmSel[1], Jump, Branch);
  or or_3 (RegWrite, IsRType, IsIType, MEMREAD, Jump);
  or or_4 (ALUSRC, IsIType, MEMWrite, MEMREAD);

  assign WBSel = {Jump, MEMREAD};

  // Other names for the same wires on the sheet: IsBranch = Branch; IsSW = MEMWrite; OP0 = opcode[0]; OP1 = opcode[1];
  //   OP2 = opcode[2]; OP3 = opcode[3]; OP4 = opcode[4]; OP5 = opcode[5]; OP6 = opcode[6]; IsLW = MEMREAD;
  //   IsJAL = Jump
endmodule

module ALUCtrl (
  input  [2:0] func3,
  input  [6:0] func7,
  input  [6:0] opcode,
  output [7:0] ALUCtrl
);

  wire and_1_out, and_2_out, and_3_out, and_4_out, and_5_out, and_6_out, and_7_out, and_8_out, and_9_out,
       and_10_out, branch, comparator_1_eq, comparator_2_eq, comparator_3_eq, comparator_4_eq,
       comparator_5_eq, comparator_6_eq, comparator_7_eq, comparator_8_eq, comparator_9_eq, jump, load,
       not_1_out, not_2_out, or_1_out, or_2_out, or_3_out, or_4_out, store;

  Comparator #(.width(3)) comparator_1 (.a(func3), .b(3'b000), .eq(comparator_1_eq));  // open: gt, lt
  Comparator #(.width(3)) comparator_2 (.a(func3), .b(3'b111), .eq(comparator_2_eq));  // open: gt, lt
  Comparator #(.width(3)) comparator_3 (.a(func3), .b(3'b110), .eq(comparator_3_eq));  // open: gt, lt
  Comparator #(.width(3)) comparator_4 (.a(func3), .b(3'b100), .eq(comparator_4_eq));  // open: gt, lt
  Comparator #(.width(3)) comparator_5 (.a(func3), .b(3'b010), .eq(comparator_5_eq));  // open: gt, lt
  Comparator #(.width(3)) comparator_6 (.a(func3), .b(3'b001), .eq(comparator_6_eq));  // open: gt, lt
  Comparator #(.width(3)) comparator_7 (.a(func3), .b(3'b101), .eq(comparator_7_eq));  // open: gt, lt
  Comparator #(.width(7)) comparator_8 (.a(opcode), .b(7'b0110011), .eq(comparator_8_eq));  // open: gt, lt
  Comparator #(.width(7)) comparator_9 (.a(opcode), .b(7'b0010011), .eq(comparator_9_eq));  // open: gt, lt
  or or_1 (or_1_out, comparator_8_eq, comparator_9_eq);
  not not_1 (not_1_out, func7[5]);
  not not_2 (not_2_out, func7[5]);
  and and_1 (and_1_out, comparator_1_eq, comparator_8_eq, func7[5]);
  and and_2 (and_2_out, comparator_8_eq, comparator_1_eq, not_1_out);
  and and_3 (and_3_out, comparator_9_eq, comparator_1_eq);
  and and_4 (and_4_out, or_1_out, comparator_2_eq);
  and and_5 (and_5_out, or_1_out, comparator_3_eq);
  and and_6 (and_6_out, or_1_out, comparator_4_eq);
  and and_7 (and_7_out, or_1_out, comparator_5_eq);
  and and_8 (and_8_out, or_1_out, comparator_6_eq);
  and and_9 (and_9_out, or_1_out, func7[5], comparator_7_eq);
  and and_10 (and_10_out, or_1_out, comparator_7_eq, not_2_out);
  or or_2 (or_2_out, and_2_out, and_3_out);
  or or_3 (or_3_out, branch, and_7_out);
  assign ALUCtrl = and_1_out ? 8'h42 : 8'bz;  // Controlled_Buffer controlled_buffer_1
  assign ALUCtrl = or_4_out ? 8'h2 : 8'bz;  // Controlled_Buffer controlled_buffer_2
  or or_4 (or_4_out, or_2_out, load, store, jump);
  assign ALUCtrl = and_4_out ? 8'h3 : 8'bz;  // Controlled_Buffer controlled_buffer_3
  assign ALUCtrl = and_5_out ? 8'h13 : 8'bz;  // Controlled_Buffer controlled_buffer_4
  assign ALUCtrl = and_6_out ? 8'h33 : 8'bz;  // Controlled_Buffer controlled_buffer_5
  assign ALUCtrl = or_3_out ? 8'h41 : 8'bz;  // Controlled_Buffer controlled_buffer_6
  assign ALUCtrl = and_8_out ? 8'h4 : 8'bz;  // Controlled_Buffer controlled_buffer_7
  assign ALUCtrl = and_9_out ? 8'hc0 : 8'bz;  // Controlled_Buffer controlled_buffer_8
  assign ALUCtrl = and_10_out ? 8'h8 : 8'bz;  // Controlled_Buffer controlled_buffer_9
  Comparator #(.width(7)) comparator_10 (.a(opcode), .b(7'b0100011), .eq(store));  // open: gt, lt
  Comparator #(.width(7)) comparator_11 (.a(opcode), .b(7'b0000011), .eq(load));  // open: gt, lt
  Comparator #(.width(7)) comparator_12 (.a(opcode), .b(7'b1100011), .eq(branch));  // open: gt, lt
  Comparator #(.width(7)) comparator_13 (.a(opcode), .b(7'b1101111), .eq(jump));  // open: gt, lt

  // Other names for the same wires on the sheet: bit30 = func7[5]
endmodule

module branchLogic (
  input  [2:0] func3,
  input  branch,
  input  jump,
  input  zeroFlag,
  output PC_src
);

  wire Beq_take, Bne_take, isBeq, isBne, not_1_out;

  Comparator #(.width(3)) comparator_1 (.a(func3), .b(3'b000), .eq(isBeq));  // open: gt, lt
  Comparator #(.width(3)) comparator_2 (.a(func3), .b(3'b001), .eq(isBne));  // open: gt, lt
  not not_1 (not_1_out, zeroFlag);
  and and_1 (Beq_take, isBeq, branch, zeroFlag);
  and and_2 (Bne_take, isBne, branch, not_1_out);
  or or_1 (PC_src, Beq_take, jump, Bne_take);
endmodule

module InstructionMemory (
  input  [31:0] Address,
  output [31:0] Instructions
);

  ROM #(.addrWidth(24), .dataWidth(32)) rom_1 (.addr(Address[25:2]), .data(Instructions));

  // Notes on the sheet:
  //   contents of rom_1 (hex, n*v repeats v):
  //   500093 500113 208463 6f00193 de00193 209463 700213 8002ef a00313 a00313
endmodule
